# Fritzing sketch Wiring (saved by Fritzing 0.9.3b)
breadboards: 1

parts:
  J1 = Piezo Speaker
  Bauteil1 = ws2812b [package="smd 2812b"]
  Bauteil2 = ws2812b [package="smd 2812b"]
  Bauteil3 = ws2812b [package="smd 2812b"]
  Bauteil4 = 0.56" 7-segment LED Backpack [part_number=1002]
  Bauteil5 = 0.56" 7-segment LED Backpack [part_number=1002]
  Bauteil6 = Adafruit HUZZAH32 ESP32 Feather [part_number="Adafruit #3405"]
  Load_Cell1 = Load Cell - Red/white/black/green
  Load_Cell2 = Load Cell - Red/white/black/green
  Touch_Button_1 = Adafruit AT42QT1010 Standalone Momentary Capacitive Touch Sensor [part_number="Adafruit #1374"]
  Touch_Button_2 = Adafruit AT42QT1010 Standalone Momentary Capacitive Touch Sensor [part_number="Adafruit #1374"]
  SparkFun_Load_Cell_Amplifier_-_HX1 = SparkFun Load Cell Amplifier - HX711 [part_number=SEN-13879]
  SparkFun_Load_Cell_Amplifier_-_HX2 = SparkFun Load Cell Amplifier - HX711 [part_number=SEN-13879]

nets:
  GND: J1.pin1, Bauteil1.VSS, Bauteil2.VSS, Bauteil3.VSS, Bauteil4.GND, Bauteil5.GND, Bauteil6.GND, Load_Cell1.wire3, Touch_Button_1.GND, Touch_Button_2.GND, SparkFun_Load_Cell_Amplifier_-_HX2.GND
  N1: J1.pin2, Bauteil6.A0_DAC2
  VDD: Bauteil1.VDD, Bauteil2.VDD, Bauteil3.VDD, Bauteil4.VDD, Bauteil5.VDD, Bauteil6.3.3V, Touch_Button_1.VDD, Touch_Button_2.VDD
  N2: Bauteil1.DIN, Bauteil2.DOUT
  N3: Bauteil2.DIN, Bauteil3.DOUT
  N4: Bauteil3.DIN, Bauteil6.IO27_A10
  N5: Bauteil4.SCL, Bauteil5.SCL, Bauteil6.SCL
  N6: Bauteil4.SDA, Bauteil5.SDA, Bauteil6.SDA
  N7: Bauteil6.SCK, Touch_Button_2.OUT
  N8: Bauteil6.A1_DAC1, Touch_Button_2.LEDA
  N9: Bauteil6.IO13_A12, Touch_Button_1.OUT
  N10: Bauteil6.IO12_A11, Touch_Button_1.LEDA
  N11: Load_Cell1.wire1, SparkFun_Load_Cell_Amplifier_-_HX2.AVDD
  N12: Load_Cell1.wire2, SparkFun_Load_Cell_Amplifier_-_HX2.A-
  N13: Load_Cell1.wire4, SparkFun_Load_Cell_Amplifier_-_HX2.A+
  N14: Load_Cell2.wire1, SparkFun_Load_Cell_Amplifier_-_HX1.AVDD
  N15: Load_Cell2.wire2, SparkFun_Load_Cell_Amplifier_-_HX1.A-
  N16: Load_Cell2.wire3, SparkFun_Load_Cell_Amplifier_-_HX1.GND
  N17: Load_Cell2.wire4, SparkFun_Load_Cell_Amplifier_-_HX1.A+

custom parts:
  0.56" 7-segment LED Backpack: This 0.56" 7-segment LED display includes a driver chip for simple control via an I2C interface. The backpack features address-selection jumpers so you can connect up to eight displays on a single I2C bus.
  Load Cell - Red/white/black/green: A rectangle load cell/weighting pressure Sensor with four wires - Red, white, black, green. Normally corresponding with E+, E-, A+, A- respectively.
  Adafruit AT42QT1010 Standalone Momentary Capacitive Touch Sensor: This breakout board is the simplest way to create a project with a single "momentary" capacitive touch sensor. No microcontroller is required here - just power with 1.8 to 5.5VDC and touch the pad to activate the sensor. When a capacitive load is detected (e.g. a person touches the sensor-pad area) the red LED lights up and the output pin goes high. You can also solder a wire to the middle pad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
  SparkFun Load Cell Amplifier - HX711: The SparkFun Load Cell Amplifier is a small breakout board for the HX711 IC that allows you to easily read load cells to measure weight. By connecting the amplifier to your microcontroller you will be able to read the changes in the resistance of the load cell, and with some calibration you’ll be able to get very accurate weight measurements. This can be handy for creating your own industrial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
